// Digital circuit flags.dig as structural Verilog
module flags (
  input  isCmp,
  input  is_gt,
  input  is_eq,
  output flags_GT,
  output flags_E
);

  dflipflop dflipflop_1 (.D(is_gt), .clk(isCmp), .Q(flags_GT));  // open: Q_2
  dflipflop dflipflop_2 (.D(is_eq), .clk(isCmp), .Q(flags_E));  // open: Q_2
endmodule
